# Fritzing sketch aelcd_example (saved by Fritzing 0.4.3b)
breadboards: 1

parts:
  LCD1 = LCD screen
  Arduino1 = Arduino
  R1 = Trimmer Potentiometer [package=THT]

nets:
  VSS: LCD1.VSS, LCD1.LED-, Arduino1.GND, R1.leg1
  N1: LCD1.VDD, Arduino1.D11
  N2: LCD1.V0, R1.wiper
  N3: LCD1.RS, Arduino1.D10
  N4: LCD1.R/W, Arduino1.D9
  N5: LCD1.E, Arduino1.D8
  N6: LCD1.DB4, Arduino1.A0
  N7: LCD1.DB5, Arduino1.A1
  N8: LCD1.DB6, Arduino1.A2
  N9: LCD1.DB7, Arduino1.A3
  N10: LCD1.LED+, Arduino1.+5V, R1.leg2

notes:
  Yellow lines are the "control bus". From right to left {EN, RW, RS}.
  The blue pin is used to power cycle the LCD controller, as the arduino initialisation sequence can screw up the LCD configuration.
  POT controls contrast
  Green pins are the data bus, operating in 4 bit mode, so as to save precious AVR pins.
  Download code from:
  http://theunixzoo.co.uk/
